# Fritzing sketch LCD Connections (saved by Fritzing 0.8.3b)

parts:
  RaspberryPi1 = Raspberry Pi Model B
  U1 = LCD-16X2 [package=lcd-16x2]

nets:
  3V3: RaspberryPi1.3V3, RaspberryPi1.5V, U1.VDD
  GND: RaspberryPi1.SCL, RaspberryPi1.GND, U1.VSS, U1.R_W
  N1: RaspberryPi1.#17, U1.DB0
  N2: RaspberryPi1.#18, U1.DB1
  N3: RaspberryPi1.#21, U1.DB2
  N4: RaspberryPi1.#22, U1.DB3
  N5: RaspberryPi1.SCLK, RaspberryPi1.CS0, U1.E
  N6: RaspberryPi1.CS1, U1.RS

custom parts:
  Raspberry Pi Model B: Raspberry Pi (Model B)
